# Fritzing sketch TrafficLight (saved by Fritzing 0.9.4)
circuit board: 1.5509cm x 5.02853cm
breadboards: 1

parts:
  LED1 = LED - 5mm [color="Red (633nm)" package="5 mm [THT]"]
  LED2 = LED - 5mm [color="Yellow (592nm)" package="5 mm [THT]"]
  LED3 = LED - 5mm [color="Green (555nm)" package="5 mm [THT]"]
  R1 = Resistor [tolerance=±5% resistance=220 package=THT]
  R2 = Resistor [tolerance=±5% resistance=220 package=THT]
  R3 = Resistor [tolerance=±5% resistance=100 package=THT]
  PINs = female pin header, 4 pins [form="♀ (female)"]

nets:
  N1: LED1.cathode, LED2.cathode, LED3.cathode, PINs.pin1
  N2: LED1.anode, R1.Pin_1
  N3: LED2.anode, R2.Pin_1
  N4: LED3.anode, R3.Pin_1
  N5: R1.Pin_0, PINs.pin4
  N6: R2.Pin_0, PINs.pin3
  N7: R3.Pin_0, PINs.pin2
