# Fritzing sketch TrafficLightController (saved by Fritzing 0.9.4)
circuit board: 5.63264cm x 3.81254cm
breadboards: 1

parts:
  Arduino_Nano = Arduino Nano (Rev3.0)
  TL_1 = female pin header, 4 pins [form="♀ (female)"]
  TL_2 = female pin header, 4 pins [form="♀ (female)"]
  TL_3 = female pin header, 4 pins [form="♀ (female)"]
  TL_4 = female pin header, 4 pins [form="♀ (female)"]
  VIN = Header 2 [package=jst-2-pth-ns]
  Maint = female pin header, 2 pins [form="♀ (female)"]
  SW1 = DIP SWITCH [package=dipswitch-02]

nets (from the pcb view):
  N1: Arduino_Nano.GND, TL_1.pin4, TL_2.pin4, TL_3.pin1, TL_4.pin1, VIN.1, Maint.pin2, SW1.1, SW1.2
  N2: Arduino_Nano.D2, SW1.4
  N3: Arduino_Nano.D3, SW1.3
  N4: Arduino_Nano.D4, TL_3.pin2
  N5: Arduino_Nano.D5, TL_3.pin3
  N6: Arduino_Nano.D6, TL_3.pin4
  N7: Arduino_Nano.D7, Maint.pin1
  N8: Arduino_Nano.D8, TL_4.pin2
  N9: Arduino_Nano.D9, TL_4.pin3
  N10: Arduino_Nano.D10, TL_4.pin4
  N11: Arduino_Nano.VIN, VIN.2
  N12: Arduino_Nano.A5, TL_2.pin1
  N13: Arduino_Nano.A4, TL_2.pin2
  N14: Arduino_Nano.A3, TL_2.pin3
  N15: Arduino_Nano.A2, TL_1.pin1
  N16: Arduino_Nano.A1, TL_1.pin2
  N17: Arduino_Nano.A0, TL_1.pin3
